# Fritzing sketch pcb_001 (saved by Fritzing 0.9.6b)
circuit board: 10cm x 7.5cm

parts:
  U01 = PCF8574 [package="DIP16 [THT]"]
  J4 = double row male pin header, 6 pins [form="♂ (male)"]
  U02 = TLP620-4 [package="DIP (Dual Inline) [THT]"]
  J5 = male pin header, 4 pins [form="♂ (male)"]
  U05 = TLP620-4 [package="DIP (Dual Inline) [THT]"]
  U04 = PCF8574 [package="DIP16 [THT]"]
  U06 = TLP620-4 [package="DIP (Dual Inline) [THT]"]
  J9 = double row male pin header, 6 pins [form="♂ (male)"]
  U08 = TLP620-4 [package="DIP (Dual Inline) [THT]"]
  U11 = TLP620-4 [package="DIP (Dual Inline) [THT]"]
  U07 = PCF8574 [package="DIP16 [THT]"]
  U10 = PCF8574 [package="DIP16 [THT]"]
  J10 = double row male pin header, 6 pins [form="♂ (male)"]
  J11 = double row male pin header, 6 pins [form="♂ (male)"]
  U09 = TLP620-4 [package="DIP (Dual Inline) [THT]"]
  J107 = male pin header, 5 pins [form="♂ (male)"]
  J105 = male pin header, 5 pins [form="♂ (male)"]
  J103 = male pin header, 5 pins [form="♂ (male)"]
  J101 = male pin header, 5 pins [form="♂ (male)" part_number=5556.05A]
  R21 = Resistor [tolerance=±5% power=0.25 resistance=22 package=THT]
  R22 = Resistor [tolerance=±5% power=0.25 resistance=22 package=THT]
  R23 = Resistor [tolerance=±5% power=0.25 resistance=22 package=THT]
  R24 = Resistor [tolerance=±5% power=0.25 resistance=22 package=THT]
  R25 = Resistor [tolerance=±5% power=0.25 resistance=22 package=THT]
  R26 = Resistor [tolerance=±5% power=0.25 resistance=22 package=THT]
  R27 = Resistor [tolerance=±5% power=0.25 resistance=22 package=THT]
  R28 = Resistor [tolerance=±5% power=0.25 resistance=22 package=THT]
  R29 = Resistor [tolerance=±5% power=0.25 resistance=22 package=THT]
  R30 = Resistor [tolerance=±5% power=0.25 resistance=22 package=THT]
  R31 = Resistor [tolerance=±5% power=0.25 resistance=22 package=THT]
  R32 = Resistor [tolerance=±5% power=0.25 resistance=22 package=THT]
  R33 = Resistor [tolerance=±5% power=0.25 resistance=22 package=THT]
  R34 = Resistor [tolerance=±5% power=0.25 resistance=220 package=THT]
  R35 = Resistor [tolerance=±5% power=0.25 resistance=22 package=THT]
  R36 = Resistor [tolerance=±5% power=0.25 resistance=22 package=THT]
  J108 = male pin header, 5 pins [form="♂ (male)"]
  J106 = male pin header, 5 pins [form="♂ (male)"]
  J104 = male pin header, 5 pins [form="♂ (male)"]
  J102 = male pin header, 5 pins [form="♂ (male)"]
  R37 = Resistor [tolerance=±5% power=0.25 resistance=220 package=THT]
  R38 = Resistor [tolerance=±5% power=0.25 resistance=220 package=THT]
  R39 = Resistor [tolerance=±5% power=0.25 resistance=220 package=THT]
  R40 = Resistor [tolerance=±5% power=0.25 resistance=220 package=THT]
  R41 = Resistor [tolerance=±5% power=0.25 resistance=22 package=THT]
  R42 = Resistor [tolerance=±5% power=0.25 resistance=220 package=THT]
  R43 = Resistor [tolerance=±5% power=0.25 resistance=22 package=THT]
  R44 = Resistor [tolerance=±5% power=0.25 resistance=22 package=THT]
  R45 = Resistor [tolerance=±5% power=0.25 resistance=22 package=THT]
  R46 = Resistor [tolerance=±5% power=0.25 resistance=220 package=THT]
  R47 = Resistor [tolerance=±5% power=0.25 resistance=22 package=THT]
  R48 = Resistor [tolerance=±5% power=0.25 resistance=22 package=THT]
  R49 = Resistor [tolerance=±5% power=0.25 resistance=22 package=THT]
  R50 = Resistor [tolerance=±5% power=0.25 resistance=22 package=THT]
  R51 = Resistor [tolerance=±5% power=0.25 resistance=22 package=THT]
  R52 = Resistor [tolerance=±5% power=0.25 resistance=22 package=THT]
  J26 = male pin header, 4 pins [form="♂ (male)"]
  U12 = TLP620-4 [package="DIP (Dual Inline) [THT]"]
  U03 = TLP620-4 [package="DIP (Dual Inline) [THT]"]
  J27 = male pin header, 2 pins [form="♂ (male)"]
  R101 = IC, SIP package, 5 pins [chip_label=R part_number=4x470ohm]
  R102 = IC, SIP package, 5 pins [chip_label=R part_number=4x470ohm]
  R103 = IC, SIP package, 5 pins [chip_label=R part_number=4x470ohm]
  R104 = IC, SIP package, 5 pins [chip_label=R part_number=4x470ohm]
  R105 = IC, SIP package, 5 pins [chip_label=R part_number=4x470ohm]
  R106 = IC, SIP package, 5 pins [chip_label=R part_number=4x470ohm]
  R107 = IC, SIP package, 5 pins [chip_label=R part_number=4x470ohm]
  R108 = IC, SIP package, 5 pins [chip_label=R part_number=4x470ohm]
  J28 = male pin header, 2 pins [form="♂ (male)"]
  R201 = IC, SIP package, 8 pins [chip_label=R part_number="7x2K2 ohm"]
  R202 = IC, SIP package, 8 pins [chip_label=R part_number="7x2K2 ohm"]
  R203 = IC, SIP package, 8 pins [chip_label=R part_number="7x2K2 ohm"]
  R204 = IC, SIP package, 8 pins [chip_label=R part_number="7x2K2 ohm"]
  R301 = IC, SIP package, 5 pins [chip_label=R part_number="4x2K2 ohm"]
  R302 = IC, SIP package, 5 pins [chip_label=R part_number="4x2K2 ohm"]
  R303 = IC, SIP package, 5 pins [chip_label=R part_number="4x2K2 ohm"]
  R304 = IC, SIP package, 5 pins [chip_label=R part_number="4x2K2 ohm"]

nets:
  N1: U01.A0, J4.pin6, R204.pin2
  N2: U01.A1, J4.pin5, R204.pin3
  N3: U01.A2, J4.pin4, R204.pin4
  L02-16: U01.P0, U02.pin16, R204.pin5
  L02-14: U01.P1, U02.pin14, R204.pin6
  L02-12: U01.P2, U02.pin12, R204.pin7
  L02-10: U01.P3, U02.pin10, R204.pin8
  GND: U01.GND, J4.pin1, J4.pin2, J4.pin3, U02.pin9, U02.pin11, U02.pin13, U02.pin15, J5.pin4, U05.pin9, U05.pin11, U05.pin13, U05.pin15, U04.GND, U06.pin9, U06.pin11, U06.pin13, U06.pin15, J9.pin1, J9.pin2, J9.pin3, U08.pin9, U08.pin11, U08.pin13, U08.pin15, U11.pin9, U11.pin11, U11.pin13, U11.pin15, U07.GND, U10.GND, J10.pin1, J10.pin2, J10.pin3, J11.pin1, J11.pin2, J11.pin3, U09.pin9, U09.pin11, U09.pin13, U09.pin15, J26.pin4, U12.pin9, U12.pin11, U12.pin13, U12.pin15, U03.pin9, U03.pin11, U03.pin13, U03.pin15
  L03-16: U01.P4, U03.pin16, R304.pin2
  L03-14: U01.P5, U03.pin14, R304.pin3
  L03-12: U01.P6, U03.pin12, R304.pin4
  L03-10: U01.P7, U03.pin10, R304.pin5
  I2C-SCL: U01.SCL, J5.pin3, U04.SCL, U07.SCL, U10.SCL, J26.pin3
  I2C-SDA: U01.SDA, J5.pin2, U04.SDA, U07.SDA, U10.SDA, J26.pin2
  3.3V: U01.VCC, J5.pin1, U04.VCC, U07.VCC, U10.VCC, J26.pin1, R201.pin1, R202.pin1, R203.pin1, R204.pin1, R301.pin1, R302.pin1, R303.pin1, R304.pin1
  N4: U02.pin1, R33.Pin_1
  L27-2: U02.pin2, U02.pin4, U02.pin6, U02.pin8, U05.pin2, U05.pin4, U05.pin6, U05.pin8, U08.pin2, U08.pin4, U08.pin6, U08.pin8, U11.pin2, U11.pin4, U11.pin6, U11.pin8, J107.pin1, J105.pin1, J103.pin1, J101.pin1, J27.pin1, J27.pin2, R101.pin1, R103.pin1, R105.pin1, R107.pin1
  N5: U02.pin3, R34.Pin_1
  N6: U02.pin5, R35.Pin_1
  N7: U02.pin7, R36.Pin_1
  N8: U05.pin1, R24.Pin_1
  N9: U05.pin3, R23.Pin_1
  N10: U05.pin5, R22.Pin_1
  N11: U05.pin7, R21.Pin_1
  L05-10: U05.pin10, U04.P3, R203.pin8
  L05-12: U05.pin12, U04.P2, R203.pin7
  L05-14: U05.pin14, U04.P1, R203.pin6
  L05-16: U05.pin16, U04.P0, R203.pin5
  N12: U04.A0, J9.pin6, R203.pin2
  N13: U04.A1, J9.pin5, R203.pin3
  N14: U04.A2, J9.pin4, R203.pin4
  L06-16: U04.P4, U06.pin16, R303.pin2
  L06-14: U04.P5, U06.pin14, R303.pin3
  L06-12: U04.P6, U06.pin12, R303.pin4
  L06-10: U04.P7, U06.pin10, R303.pin5
  N15: U06.pin1, R45.Pin_1
  N16: U06.pin2, U06.pin4, U06.pin6, U06.pin8, U09.pin2, U09.pin4, U09.pin6, U09.pin8, J108.pin1, J106.pin1, J104.pin1, J102.pin1, U12.pin2, U12.pin4, U12.pin6, U12.pin8, U03.pin2, U03.pin4, U03.pin6, U03.pin8, R102.pin1, R104.pin1, R106.pin1, R108.pin1, J28.pin1, J28.pin2
  N17: U06.pin3, R46.Pin_1
  N18: U06.pin5, R47.Pin_1
  N19: U06.pin7, R48.Pin_1
  N20: U08.pin1, R25.Pin_1
  N21: U08.pin3, R26.Pin_1
  N22: U08.pin5, R27.Pin_1
  N23: U08.pin7, R28.Pin_1
  L08-10: U08.pin10, U07.P3, R202.pin8
  L08-12: U08.pin12, U07.P2, R202.pin7
  L08-14: U08.pin14, U07.P1, R202.pin6
  L08-16: U08.pin16, U07.P0, R202.pin5
  N24: U11.pin1, R29.Pin_1
  N25: U11.pin3, R30.Pin_1
  N26: U11.pin5, R31.Pin_1
  N27: U11.pin7, R32.Pin_1
  L107-10: U11.pin10, U10.P3, R201.pin8
  L107-12: U11.pin12, U10.P2, R201.pin7
  L107-14: U11.pin14, U10.P1, R201.pin6
  L107-16: U11.pin16, U10.P0, R201.pin5
  N28: U07.A0, J10.pin6, R202.pin2
  N29: U07.A1, J10.pin5, R202.pin3
  N30: U07.A2, J10.pin4, R202.pin4
  L09-16: U07.P4, U09.pin16, R302.pin2
  L09-14: U07.P5, U09.pin14, R302.pin3
  L09-12: U07.P6, U09.pin12, R302.pin4
  L09-10: U07.P7, U09.pin10, R302.pin5
  N31: U10.A0, J11.pin6, R201.pin2
  N32: U10.A1, J11.pin5, R201.pin3
  N33: U10.A2, J11.pin4, R201.pin4
  L17-16: U10.P4, U12.pin16, R301.pin2
  L17-14: U10.P5, U12.pin14, R301.pin3
  L17-12: U10.P6, U12.pin12, R301.pin4
  L17-10: U10.P7, U12.pin10, R301.pin5
  N34: U09.pin1, R41.Pin_1
  N35: U09.pin3, R42.Pin_1
  N36: U09.pin5, R43.Pin_1
  N37: U09.pin7, R44.Pin_1
  N38: J107.pin2, R29.Pin_0, R101.pin2
  N39: J107.pin3, R30.Pin_0, R101.pin3
  N40: J107.pin4, R31.Pin_0, R101.pin4
  N41: J107.pin5, R32.Pin_0, R101.pin5
  N42: J105.pin2, R25.Pin_0, R103.pin2
  N43: J105.pin3, R26.Pin_0, R103.pin3
  N44: J105.pin4, R27.Pin_0, R103.pin4
  N45: J105.pin5, R28.Pin_0, R103.pin5
  N46: J103.pin2, R24.Pin_0, R105.pin2
  N47: J103.pin3, R23.Pin_0, R105.pin3
  N48: J103.pin4, R22.Pin_0, R105.pin4
  N49: J103.pin5, R21.Pin_0, R105.pin5
  N50: J101.pin2, R33.Pin_0, R107.pin2
  N51: J101.pin3, R34.Pin_0, R107.pin3
  N52: J101.pin4, R35.Pin_0, R107.pin4
  N53: J101.pin5, R36.Pin_0, R107.pin5
  N54: J108.pin2, R37.Pin_0, R102.pin2
  N55: J108.pin3, R38.Pin_0, R102.pin3
  N56: J108.pin4, R39.Pin_0, R102.pin4
  N57: J108.pin5, R40.Pin_0, R102.pin5
  N58: J106.pin2, R41.Pin_0, R104.pin2
  N59: J106.pin3, R42.Pin_0, R104.pin3
  N60: J106.pin4, R43.Pin_0, R104.pin4
  N61: J106.pin5, R44.Pin_0, R104.pin5
  N62: J104.pin2, R45.Pin_0, R106.pin2
  N63: J104.pin3, R46.Pin_0, R106.pin3
  N64: J104.pin4, R47.Pin_0, R106.pin4
  N65: J104.pin5, R48.Pin_0, R106.pin5
  N66: J102.pin2, R49.Pin_0, R108.pin2
  N67: J102.pin3, R50.Pin_0, R108.pin3
  N68: J102.pin4, R51.Pin_0, R108.pin4
  N69: J102.pin5, R52.Pin_0, R108.pin5
  N70: R37.Pin_1, U12.pin1
  N71: R38.Pin_1, U12.pin3
  N72: R39.Pin_1, U12.pin5
  N73: R40.Pin_1, U12.pin7
  N74: R49.Pin_1, U03.pin1
  N75: R50.Pin_1, U03.pin3
  N76: R51.Pin_1, U03.pin5
  N77: R52.Pin_1, U03.pin7

notes:
  Svenn-Erik K. Thomsen
  sekt1953@gmail.com
  3V3
  SDA
  SCL
  GND
  I2C
  TrackSensor v3.0

custom parts:
  TLP620-4: Quad Photo-transistor optically coupled to two infrared emitting diodes connected in inverse parallel.
